# Fritzing sketch diagram (saved by Fritzing 0.9.6b)
breadboards: 1

parts:
  Teensy1 = Teensy 2.0
  S1 = Momentary Switch [package=tactile_switch_smd]
  LED1 = LED - 3mm [color="Red (633nm)" package="3 mm [THT]"]

nets:
  N1: Teensy1.GND, S1.1, LED1.anode
  N2: Teensy1.B1, LED1.cathode
  N3: Teensy1.B3, S1.4
